// Logisim project Turing.circ as structural Verilog: 9 circuits, main circuit main
module main (
);

  wire addrdec_1_count, addrdec_1_in_out, addrdec_1_ram, addrdec_1_reg0, addrdec_1_reg1, addrdec_1_reg2,
       addrdec_1_reg3, addrdec_1_reg4, addrdec_1_reg5, addrdec_1_stack, addrdec_2_count, addrdec_2_in_out,
       addrdec_2_ram, addrdec_2_reg0, addrdec_2_reg1, addrdec_2_reg2, addrdec_2_reg3, addrdec_2_reg4,
       addrdec_2_reg5, addrdec_2_stack, addrdec_3_count, addrdec_3_in_out, addrdec_3_ram, addrdec_3_reg0,
       addrdec_3_reg1, addrdec_3_reg2, addrdec_3_reg3, addrdec_3_reg4, addrdec_3_reg5, addrdec_3_stack,
       and_1_out, and_2_out, and_3_out, and_4_out, and_5_out, and_6_out, clock_1_out, comparator_1_gt,
       cond_1_out_4, dec_1_cal, dec_1_def, dec_1_if, dec_1_imm1, dec_1_imm2, dec_1_ram, dec_1_regban,
       or_1_out, or_2_out, or_3_out, or_4_out, or_5_out, or_6_out, or_7_out;
  wire [2:0] rom_1_data_2;
  wire [7:0] adder_1_out, alu_1_out, controlled_buffer_1_out, controlled_buffer_2_out, counter_1_q,
       counter_2_q, dualram_1_data_out3, multiplexer_1_out, rom_2_data, ticker_1_output;
  wire [31:0] rom_1_data;

  Clock clock_1 (.out(clock_1_out));
  or or_1 (or_1_out, or_2_out, addrdec_1_count);
  Ticker ticker_1 (
    .Inc(8'h1), .Output(ticker_1_output), .Replace(or_1_out), .Data(dualram_1_data_out3), .clock(clock_1_out));
  assign controlled_buffer_1_out = addrdec_2_count ? ticker_1_output : 8'bz;  // Controlled_Buffer controlled_buffer_1
  assign controlled_buffer_2_out = addrdec_3_count ? ticker_1_output : 8'bz;  // Controlled_Buffer controlled_buffer_2
  Adder adder_1 (.a(8'h4), .b(ticker_1_output), .out(adder_1_out));  // open: cin, cout
  DualRAM dualram_1 (
    .data_In1(controlled_buffer_1_out), .data_In2(controlled_buffer_2_out), .data_In3(dualram_1_data_out3),
    .Out1(addrdec_2_ram), .Out2(addrdec_3_ram), .In3(addrdec_1_ram), .set(dec_1_ram), .Action(rom_1_data_2),
    .data_Out1(controlled_buffer_1_out), .data_Out2(controlled_buffer_2_out),
    .data_Out3(dualram_1_data_out3), .clock(clock_1_out));  // open: select, clear
  or or_2 (or_2_out, dec_1_def, and_4_out);
  ROM #(.dataWidth(32)) rom_1 (
    .addr(ticker_1_output), .data({rom_1_data[31:27], rom_1_data_2, rom_1_data[23:0]}));  // open: sel
  assign dualram_1_data_out3 = or_3_out ? rom_1_data[7:0] : 8'bz;  // Controlled_Buffer controlled_buffer_3
  Dec dec_1 (
    .in_1({rom_1_data[31:27], rom_1_data_2}), .\if (dec_1_if), .imm1(dec_1_imm1), .imm2(dec_1_imm2),
    .cal(dec_1_cal), .def(dec_1_def), .ram(dec_1_ram), .RegBan(dec_1_regban));
  or or_3 (or_3_out, and_2_out, dec_1_if);
  and and_1 (and_1_out, or_4_out, clock_1_out);
  Counter #(.trigger("falling")) counter_1 (.Q(counter_1_q), .clk(and_1_out));  // open: load, D, count, carry, clr
  Stack stack_1 (
    .In(and_2_out), .Out(and_3_out), .Data_In(adder_1_out), .Data_Out(dualram_1_data_out3),
    .Clock(clock_1_out));  // open: Clear
  and and_2 (and_2_out, ~rom_1_data[27], dec_1_def);  // AND_Gate
  and and_3 (and_3_out, rom_1_data[27], dec_1_def);
  AddrDec addrdec_1 (
    .RegBan(or_6_out), .stack(addrdec_1_stack), .Addr(rom_1_data[7:0]), .AddrBan(1'b0), .ram(addrdec_1_ram),
    .reg0(addrdec_1_reg0), .reg1(addrdec_1_reg1), .reg2(addrdec_1_reg2), .reg3(addrdec_1_reg3),
    .reg4(addrdec_1_reg4), .reg5(addrdec_1_reg5), .count(addrdec_1_count), .in_out(addrdec_1_in_out));
  or or_4 (or_4_out, addrdec_2_in_out, addrdec_3_in_out);
  and and_4 (and_4_out, cond_1_out_4, dec_1_if);
  or or_5 (or_5_out, dec_1_def, dec_1_if);
  or or_6 (or_6_out, dec_1_regban, or_5_out);
  and and_5 (and_5_out, addrdec_1_stack, or_3_out);
  ROM rom_2 (.addr(counter_1_q), .data(rom_2_data));  // open: sel
  assign controlled_buffer_1_out = dec_1_imm1 ? rom_1_data[23:16] : 8'bz;  // Controlled_Buffer controlled_buffer_4
  AddrDec addrdec_2 (
    .RegBan(1'b0), .stack(addrdec_2_stack), .Addr(rom_1_data[23:16]), .AddrBan(dec_1_imm1),
    .ram(addrdec_2_ram), .reg0(addrdec_2_reg0), .reg1(addrdec_2_reg1), .reg2(addrdec_2_reg2),
    .reg3(addrdec_2_reg3), .reg4(addrdec_2_reg4), .reg5(addrdec_2_reg5), .count(addrdec_2_count),
    .in_out(addrdec_2_in_out));
  assign controlled_buffer_1_out = addrdec_2_in_out ? rom_2_data : 8'bz;  // Controlled_Buffer controlled_buffer_5
  assign controlled_buffer_2_out = dec_1_imm2 ? rom_1_data[15:8] : 8'bz;  // Controlled_Buffer controlled_buffer_6
  AddrDec addrdec_3 (
    .RegBan(1'b0), .stack(addrdec_3_stack), .Addr(rom_1_data[15:8]), .AddrBan(dec_1_imm2),
    .ram(addrdec_3_ram), .reg0(addrdec_3_reg0), .reg1(addrdec_3_reg1), .reg2(addrdec_3_reg2),
    .reg3(addrdec_3_reg3), .reg4(addrdec_3_reg4), .reg5(addrdec_3_reg5), .count(addrdec_3_count),
    .in_out(addrdec_3_in_out));
  DualRegester dualregester_1 (
    .In(dualram_1_data_out3), .Ctrl1(addrdec_2_reg0), .Ctrl2(addrdec_3_reg0), .Out1(controlled_buffer_1_out),
    .Out2(controlled_buffer_2_out), .enable(addrdec_1_reg0), .clock(clock_1_out));  // open: Out0, clean
  DualRegester dualregester_2 (
    .In(dualram_1_data_out3), .Ctrl1(addrdec_2_reg1), .Ctrl2(addrdec_3_reg1), .Out1(controlled_buffer_1_out),
    .Out2(controlled_buffer_2_out), .enable(addrdec_1_reg1), .clock(clock_1_out));  // open: Out0, clean
  DualRegester dualregester_3 (
    .In(dualram_1_data_out3), .Ctrl1(addrdec_2_reg2), .Ctrl2(addrdec_3_reg2), .Out1(controlled_buffer_1_out),
    .Out2(controlled_buffer_2_out), .enable(addrdec_1_reg2), .clock(clock_1_out));  // open: Out0, clean
  DualRegester dualregester_4 (
    .In(dualram_1_data_out3), .Ctrl1(addrdec_2_reg3), .Ctrl2(addrdec_3_reg3), .Out1(controlled_buffer_1_out),
    .Out2(controlled_buffer_2_out), .enable(addrdec_1_reg3), .clock(clock_1_out));  // open: Out0, clean
  DualRegester dualregester_5 (
    .In(dualram_1_data_out3), .Ctrl1(addrdec_2_reg4), .Ctrl2(addrdec_3_reg4), .Out1(controlled_buffer_1_out),
    .Out2(controlled_buffer_2_out), .enable(addrdec_1_reg4), .clock(clock_1_out));  // open: Out0, clean
  DualRegester dualregester_6 (
    .In(dualram_1_data_out3), .Ctrl1(addrdec_2_reg5), .Ctrl2(addrdec_3_reg5), .Out1(controlled_buffer_1_out),
    .Out2(controlled_buffer_2_out), .enable(addrdec_1_reg5), .clock(clock_1_out));  // open: Out0, clean
  assign controlled_buffer_2_out = addrdec_3_in_out ? rom_2_data : 8'bz;  // Controlled_Buffer controlled_buffer_7
  Cond cond_1 (
    .in_2(controlled_buffer_1_out), .in_3(controlled_buffer_2_out), .out_4(cond_1_out_4), .in_1(rom_1_data_2));
  Alu alu_1 (.in1(controlled_buffer_1_out), .in2(controlled_buffer_2_out), .out(alu_1_out), .Opcode(rom_1_data_2));
  assign dualram_1_data_out3 = dec_1_cal ? alu_1_out : 8'bz;  // Controlled_Buffer controlled_buffer_8
  Counter #(.trigger("falling")) counter_2 (.Q(counter_2_q), .clk(and_6_out));  // open: load, D, count, carry, clr
  TTY tty_1 (.data(dualram_1_data_out3[6:0]), .clk(and_6_out), .we(comparator_1_gt));  // open: clr
  and and_6 (and_6_out, addrdec_1_in_out, clock_1_out);
  or or_7 (or_7_out, addrdec_2_stack, addrdec_3_stack);
  Multiplexer #(.width(8)) multiplexer_1 (
    .in0(controlled_buffer_1_out), .in1(controlled_buffer_2_out), .out(multiplexer_1_out),
    .en(addrdec_3_stack));  // open: sel
  Comparator #(.width(7), .mode("unsigned")) comparator_1 (
    .a(dualram_1_data_out3[6:0]), .b(7'b0101111), .gt(comparator_1_gt));  // open: eq, lt
  Stack stack_2 (
    .In(and_5_out), .Out(or_7_out), .Data_In(multiplexer_1_out), .Data_Out(dualram_1_data_out3),
    .Clock(clock_1_out));  // open: Clear
  RAM ram_1 (.addr(counter_2_q), .data(dualram_1_data_out3), .clk(and_6_out), .ld(1'b0));  // open: sel, clr

  // Notes on the sheet:
  //   contents of rom_1 (hex, n*v repeats v):
  //   80070000 22000203 80000002 f010000 80011001 f010200 81010f01 a2011000 81010101 8c010002 80011001
  //   f010200 81011101 8c010000 22000210 80000002 80011001 8c010000 25020014 f010200 81011101 a201800d
  //   c0000000 c0000001 80011002 8020100 1808000 30003 80010101 a2011018 80030007
  //   contents of rom_2 (hex, n*v repeats v):
  //   11 2 3 4 5 6 7 8 9 a b c d e f 10
endmodule

module DualRegester (
  input  enable,
  input  [7:0] In,
  input  Ctrl1,
  input  Ctrl2,
  input  clock,
  input  clean,
  output [7:0] Out0,
  output [7:0] Out1,
  output [7:0] Out2
);

  Register #(.trigger("falling")) register_1 (.D(In), .en(enable), .Q(Out0), .clk(clock), .clr(clean));
  assign Out1 = Ctrl1 ? Out0 : 8'bz;  // Controlled_Buffer controlled_buffer_1
  assign Out2 = Ctrl2 ? Out0 : 8'bz;  // Controlled_Buffer controlled_buffer_2
endmodule

module Dec (
  input  [7:0] in_1,
  output def,
  output \if ,
  output imm1,
  output imm2,
  output cal,
  output ram,
  output RegBan
);

  wire github_67_99_out, not_1_out, not_2_out, not_3_out, not_4_out;

  and and_1 (def, in_1[5], in_1[4]);
  not not_1 (not_1_out, in_1[4]);
  not not_2 (not_2_out, in_1[3]);
  not not_3 (not_3_out, in_1[4]);
  not github_67_99 (github_67_99_out, in_1[5]);
  and and_2 (ram, github_67_99_out, not_3_out, in_1[3]);
  not not_4 (not_4_out, in_1[2]);
  and and_3 (RegBan, ram, not_4_out);
  and and_4 (\if , in_1[5], not_1_out, not_2_out);
  nor nor_1 (cal, in_1[3], in_1[5]);

  assign imm1 = in_1[6];
  assign imm2 = in_1[7];
endmodule

module AddrDec (
  input  [7:0] Addr,
  input  AddrBan,
  input  RegBan,
  output stack,
  output count,
  output ram,
  output reg0,
  output reg1,
  output reg2,
  output reg3,
  output reg4,
  output reg5,
  output in_out
);

  wire decoder_1_out0, decoder_1_out1, decoder_1_out2, decoder_1_out3, decoder_1_out4, decoder_1_out5,
       decoder_1_out6, decoder_1_out7, nor_1_out;

  and and_1 (count, nor_1_out, decoder_1_out6);
  and and_2 (ram, ~AddrBan, Addr[7]);  // AND_Gate
  and and_3 (stack, Addr[6], ~AddrBan);  // AND_Gate
  nor nor_1 (nor_1_out, ram, stack, AddrBan, RegBan);
  and and_4 (reg2, nor_1_out, decoder_1_out2);
  and and_5 (reg1, nor_1_out, decoder_1_out1);
  and and_6 (reg0, nor_1_out, decoder_1_out0);
  Decoder #(.select(3)) decoder_1 (
    .out0(decoder_1_out0), .out1(decoder_1_out1), .out2(decoder_1_out2), .out3(decoder_1_out3),
    .out4(decoder_1_out4), .out5(decoder_1_out5), .out6(decoder_1_out6), .out7(decoder_1_out7),
    .sel(Addr[2:0]));  // open: en
  and and_7 (reg5, nor_1_out, decoder_1_out5);
  and and_8 (reg3, nor_1_out, decoder_1_out3);
  and and_9 (reg4, nor_1_out, decoder_1_out4);
  and and_10 (in_out, nor_1_out, decoder_1_out7);
endmodule

module Alu (
  input  [2:0] Opcode,
  input  [7:0] in1,
  input  [7:0] in2,
  output [7:0] out
);

  wire [7:0] adder_1_out, and_1_out, not_1_out, or_1_out, shifter_1_out, shifter_2_out, subtractor_1_out,
       xor_1_out;

  Adder adder_1 (.a(in1), .b(in2), .out(adder_1_out));  // open: cin, cout
  Subtractor subtractor_1 (.a(in1), .b(in2), .out(subtractor_1_out));  // open: bin, bout
  assign and_1_out = in1 & in2;  // AND_Gate and_1, 8 bits wide
  assign or_1_out = in1 | in2;  // OR_Gate or_1, 8 bits wide
  assign not_1_out = ~in1;  // NOT_Gate not_1, 8 bits wide
  assign xor_1_out = in2 ^ in1;  // XOR_Gate xor_1, 8 bits wide
  Shifter shifter_1 (.in(in1), .\dist (in2[2:0]), .out(shifter_1_out));
  Shifter #(.shift("lr")) shifter_2 (.in(in1), .\dist (in2[2:0]), .out(shifter_2_out));
  Multiplexer #(.select(3), .width(8)) multiplexer_1 (
    .in0(adder_1_out), .in1(subtractor_1_out), .in2(and_1_out), .in3(or_1_out), .in4(not_1_out),
    .in5(xor_1_out), .in6(shifter_1_out), .in7(shifter_2_out), .out(out), .sel(Opcode));  // open: en
endmodule

module Cond (
  input  [2:0] in_1,
  input  [7:0] in_2,
  input  [7:0] in_3,
  output out_4
);

  wire and_1_out, and_2_out, and_3_out, comparator_1_eq, comparator_1_gt, comparator_1_lt, nor_1_out;

  Comparator #(.mode("unsigned")) comparator_1 (
    .a(in_2), .b(in_3), .gt(comparator_1_gt), .eq(comparator_1_eq), .lt(comparator_1_lt));
  and and_1 (and_1_out, in_1[2], comparator_1_gt);
  and and_2 (and_2_out, in_1[0], comparator_1_eq);
  and and_3 (and_3_out, comparator_1_lt, in_1[1]);
  nor nor_1 (nor_1_out, in_1[0], in_1[1], in_1[2], comparator_1_eq);
  or or_1 (out_4, nor_1_out, and_1_out, and_2_out, and_3_out);
endmodule

module Ticker (
  input  Replace,
  input  [7:0] Inc,
  input  [7:0] Data,
  input  clock,
  output [7:0] Output
);

  wire [7:0] adder_1_out, multiplexer_1_out;

  Adder adder_1 (.a(Output), .b(Inc), .out(adder_1_out));  // open: cin, cout
  Multiplexer #(.width(8)) multiplexer_1 (
    .in0(adder_1_out), .in1(Data), .out(multiplexer_1_out), .sel(Replace));  // open: en
  Register #(.trigger("falling")) register_1 (.D(multiplexer_1_out), .en(1'b1), .Q(Output), .clk(clock));  // open: clr
endmodule

module Stack (
  input  [7:0] Data_In,
  input  In,
  input  Out,
  input  Clock,
  input  Clear,
  output [7:0] Data_Out
);

  wire and_1_out, or_1_out, subtractor_1_bout;
  wire [7:0] adder_1_out, multiplexer_1_out, multiplexer_2_out, multiplexer_3_out, ram_1_data, register_1_q,
       subtractor_1_out;

  Adder adder_1 (.a(register_1_q), .b(8'h1), .out(adder_1_out));  // open: cin, cout
  Subtractor subtractor_1 (.a(register_1_q), .b(8'h1), .out(subtractor_1_out), .bout(subtractor_1_bout));  // open: bin
  Multiplexer #(.width(8)) multiplexer_1 (
    .in0(subtractor_1_out), .in1({8{1'b0}}), .out(multiplexer_1_out), .sel(subtractor_1_bout));  // open: en
  Register register_1 (.D(multiplexer_2_out), .Q(register_1_q), .clk(and_1_out), .clr(Clear));  // open: en
  Multiplexer #(.width(8)) multiplexer_2 (
    .in0(adder_1_out), .in1(multiplexer_1_out), .out(multiplexer_2_out), .sel(Out));  // open: en
  and and_1 (and_1_out, or_1_out, Clock);
  or or_1 (or_1_out, In, Out);
  Multiplexer #(.width(8)) multiplexer_3 (
    .in0(register_1_q), .in1(multiplexer_1_out), .out(multiplexer_3_out), .sel(Out));  // open: en
  RAM ram_1 (.addr(multiplexer_3_out), .data(ram_1_data), .clk(Clock), .ld(Out), .clr(Clear));  // open: sel
  assign ram_1_data = In ? Data_In : 8'bz;  // Controlled_Buffer controlled_buffer_1
  assign Data_Out = Out ? ram_1_data : 8'bz;  // Controlled_Buffer controlled_buffer_2
endmodule

module DualRAM (
  input  set,
  input  [2:0] Action,
  input  Out1,
  input  Out2,
  input  [7:0] data_In1,
  input  [7:0] data_In2,
  input  In3,
  input  [7:0] data_In3,
  input  select,
  input  clock,
  input  clear,
  output [7:0] data_Out1,
  output [7:0] data_Out3,
  output [7:0] data_Out2
);

  wire and_1_out, and_2_out, and_3_out, and_4_out, and_5_out, multiplexer_2_out, nand_1_out, nand_2_out,
       nor_1_out, not_1_out, not_2_out, not_3_out, or_1_out, Out1State_qn, Out2State_qn, StoSto_q, undriven;
  wire [7:0] AddrSto_q, DataSto_q, multiplexer_1_out, multiplexer_3_out, multiplexer_4_out, multiplexer_6_out;

  not not_1 (not_1_out, Action[2]);
  not not_2 (not_2_out, Action[0]);
  and and_1 (and_1_out, not_1_out, set);
  Multiplexer #(.width(8)) multiplexer_1 (
    .in0(data_In1), .in1(data_In2), .out(multiplexer_1_out), .sel(not_2_out));  // open: en
  nand nand_1 (nand_1_out, Action[2], set);
  or or_1 (or_1_out, Action[1], Action[0]);
  Multiplexer multiplexer_2 (.in0(or_1_out), .in1(StoSto_q), .out(multiplexer_2_out), .sel(nand_1_out));  // open: en
  D_Flip_Flop StoSto (.clk(clock), .D(Action[1]), .Q(StoSto_q), .en(and_1_out), .reset(clear));  // open: Qn, preset
  Register AddrSto (.D(multiplexer_1_out), .en(and_1_out), .Q(AddrSto_q), .clk(clock), .clr(clear));
  and and_2 (and_2_out, Action[0], ~Action[2], set);  // AND_Gate
  not not_3 (not_3_out, set);
  Multiplexer #(.width(8)) multiplexer_3 (
    .in0(data_In1), .in1(AddrSto_q), .out(multiplexer_3_out), .sel(not_3_out));  // open: en
  nand nand_2 (nand_2_out, multiplexer_2_out, ~and_2_out);  // NAND_Gate
  and and_3 (and_3_out, ~Action[0], ~Action[1], Action[2], set);  // AND_Gate
  and and_4 (and_4_out, ~Action[0], Action[1], ~Action[2], set);  // AND_Gate
  and and_5 (and_5_out, ~Action[0], ~Action[2], set);  // AND_Gate
  Priority_Encoder priority_encoder_1 (
    .in0(set), .in1(select), .in3(In3), .in4(Out2), .in5(Out1), .in7(clear));  // open: in2, in6, out, en_in
  Multiplexer #(.width(8)) multiplexer_4 (
    .in0(data_In2), .in1(data_In3), .out(multiplexer_4_out), .sel(In3), .en(nor_1_out));
  D_Flip_Flop Out2State (.clk(clock), .D(and_4_out), .Qn(Out2State_qn), .en(set));  // open: Q, preset, reset
  D_Flip_Flop Out1State (.clk(clock), .D(and_5_out), .Qn(Out1State_qn), .en(set));  // open: Q, preset, reset
  RAM ram_1 (
    .addr(multiplexer_3_out), .data(multiplexer_4_out), .sel(undriven), .clk(clock), .ld(nand_2_out),
    .clr(clear));
  nor nor_1 (nor_1_out, nand_2_out, and_5_out);
  Multiplexer #(.width(8)) multiplexer_5 (
    .in0(DataSto_q), .in1(multiplexer_6_out), .out(data_Out1), .sel(Out1State_qn), .en(Out1));
  Register DataSto (.D(multiplexer_4_out), .en(and_5_out), .Q(DataSto_q), .clk(clock), .clr(clear));
  Multiplexer #(.width(8)) multiplexer_6 (
    .in0({8{1'b0}}), .in1(multiplexer_4_out), .out(multiplexer_6_out), .sel(nand_2_out));  // open: en
  assign data_Out3 = and_3_out ? multiplexer_6_out : 8'bz;  // Controlled_Buffer controlled_buffer_1
  Multiplexer #(.width(8)) multiplexer_7 (
    .in0(DataSto_q), .in1(multiplexer_6_out), .out(data_Out2), .sel(Out2State_qn), .en(Out2));
endmodule
